# Fritzing sketch Hardware Schematic (saved by Fritzing 1.0.2b)
circuit board: 5.06777cm x 2.69528cm
breadboards: 1

parts:
  Arduino_Micro = Arduino Micro
  4x4_Button_Matrix = 4x4 Keypad [part_number=101207]

nets:
  N1: Arduino_Micro.D2, 4x4_Button_Matrix.8
  N2: Arduino_Micro.D3, 4x4_Button_Matrix.7
  N3: Arduino_Micro.D4, 4x4_Button_Matrix.6
  N4: Arduino_Micro.D5, 4x4_Button_Matrix.5
  N5: Arduino_Micro.D6, 4x4_Button_Matrix.4
  N6: Arduino_Micro.D7, 4x4_Button_Matrix.3
  N7: Arduino_Micro.D8, 4x4_Button_Matrix.2
  N8: Arduino_Micro.D9, 4x4_Button_Matrix.1

notes:
  Find the source code at
  https://github.com/quinn-n/Helldivers-2-Strategem-Controller

custom parts:
  Arduino Micro: Arduino Micro Microcontroller
  4x4 Keypad: Matrix membrane keypad 4x4
